# Fritzing sketch Test_water_sensor (saved by Fritzing 0.9.3b)

parts:
  Water_Level_Sensor = Water Level Sensor
  Part1 = Arduino Uno (Rev3)

nets:
  N1: Water_Level_Sensor.SIG, Part1.A0
  VCC: Water_Level_Sensor.VCC, Part1.5V
  GND: Water_Level_Sensor.GND, Part1.GND

custom parts:
  Water Level Sensor: A water level sensor. This sensor operates at 3V to 5V. The Sig (signal) pin outputs an analogue signal that is in proportion to the amount of water in contact with the sensor.
